# Fritzing sketch quickdraw_circuit (saved by Fritzing 0.9.3b)
breadboards: 1

parts:
  S1 = Toggle Switch [package=THT]
  J1 = Piezo Speaker
  Raspberry_Pi_1 = Raspberry Pi 3 [part_number=RPI-3-V1.2]
  IC1 = MCP3008 8-channel 10-bit ADC [part_number=MCP3008]
  S2 = Toggle Switch [package=THT]
  J2 = Piezo Speaker
  R3 = Resistor [tolerance=±5% resistance=1M package=THT]
  R4 = Resistor [tolerance=±5% resistance=1M package=THT]
  S3 = Round Pushbutton

nets:
  N1: S1.L1, Raspberry_Pi_1.5V, IC1.no_name_yet#15, IC1.no_name_yet#16, S2.L1, S3.leg0
  N2: S1.COM, IC1.no_name_yet#1
  N3: J1.pin1, Raspberry_Pi_1.GND, IC1.no_name_yet#9, IC1.no_name_yet#14, J2.pin1, R3.Pin_0, R4.Pin_0
  N4: J1.pin2, IC1.no_name_yet#4, R4.Pin_1
  N5: Raspberry_Pi_1.3V3, Raspberry_Pi_1.GPIO10, IC1.no_name_yet#11
  N6: Raspberry_Pi_1.GPIO9, IC1.no_name_yet#12
  N7: Raspberry_Pi_1.GPIO11, IC1.no_name_yet#13
  N8: Raspberry_Pi_1.GPIO8, IC1.no_name_yet#10
  N9: IC1.no_name_yet#2, S2.COM
  N10: IC1.no_name_yet#3, J2.pin2, R3.Pin_1
  N11: IC1.no_name_yet#6, S3.leg1
